// Logisim project Main_Circuit.circ as structural Verilog: 1 circuit, main circuit main
module main (
  output Stop_Lamp
);

  wire ADD, and_1_out, and_2_out, and_4_out, and_5_out, and_6_out, and_7_out, and_8_out, and_9_out,
       and_10_out, and_11_out, and_12_out, and_14_out, and_15_out, and_16_out, and_17_out, and_18_out,
       and_19_out, and_20_out, and_21_out, and_22_out, and_23_out, ANDop, branch_taken, clk, comparator_1_lt,
       CTR3_q, DIV, HLT, JMP, JRP, LDN, MUL, NEG, not_2_out, not_4_out, not_5_out, not_6_out, not_7_out,
       not_8_out, NOTop, or_3_out, or_4_out, or_6_out, or_7_out, ORop, s_r_ff_1_qn, SKN, STO, SUB, t0, t1;
  wire [15:0] adder_2_out, adder_3_out, adder_4_out, multiplexer_10_out, multiplexer_11_out,
       multiplexer_12_out, multiplexer_13_out, multiplexer_14_out, multiplexer_15_out, multiplexer_16_out,
       multiplexer_17_out, multiplexer_18_out, multiplexer_19_out, or_5_out, or_8_out, PC_q, ram_1_dout,
       ram_1_dout_2;
  wire [31:0] Acc_q, adder_1_out, and_3_out, divider_1_out, IR_q, multiplexer_1_out, multiplexer_2_out,
       multiplexer_3_out, multiplexer_4_out, multiplexer_5_out, multiplexer_6_out, multiplexer_7_out,
       multiplexer_8_out, multiplexer_9_out, multiplier_1_out, negator_1_out, not_1_out, or_1_out, or_2_out,
       subtractor_1_out;

  Clock clock_1 (.out(clk));
  and and_1 (and_1_out, HLT, t1);
  Multiplexer #(.width(32)) multiplexer_1 (
    .in0({32{1'b0}}), .in1({ram_1_dout_2, ram_1_dout}), .out(multiplexer_1_out), .sel(and_2_out));
  and and_2 (and_2_out, t1, LDN);
  Subtractor #(.width(32)) subtractor_1 (
    .a(Acc_q), .b({ram_1_dout_2, ram_1_dout}), .out(subtractor_1_out));  // open: bin, bout
  Adder #(.width(32)) adder_1 (.a(Acc_q), .b({ram_1_dout_2, ram_1_dout}), .out(adder_1_out));  // open: cin, cout
  Multiplier #(.width(32)) multiplier_1 (
    .a(Acc_q), .b({ram_1_dout_2, ram_1_dout}), .out(multiplier_1_out));  // open: cin, cout
  Divider #(.width(32)) divider_1 (.a(Acc_q), .b({ram_1_dout_2, ram_1_dout}), .out(divider_1_out));  // open: upper, rem
  Negator #(.width(32)) negator_1 (.in(Acc_q), .out(negator_1_out));
  assign and_3_out = Acc_q & {ram_1_dout_2, ram_1_dout};  // AND_Gate and_3, 32 bits wide
  assign or_1_out = Acc_q | {ram_1_dout_2, ram_1_dout};  // OR_Gate or_1, 32 bits wide
  assign not_1_out = ~Acc_q;  // NOT_Gate not_1, 32 bits wide
  Multiplexer #(.width(32)) multiplexer_2 (
    .in0({32{1'b0}}), .in1(subtractor_1_out), .out(multiplexer_2_out), .sel(and_4_out));
  and and_4 (and_4_out, t1, SUB);
  Multiplexer #(.width(32)) multiplexer_3 (
    .in0({32{1'b0}}), .in1(adder_1_out), .out(multiplexer_3_out), .sel(and_5_out));
  and and_5 (and_5_out, t1, ADD);
  Multiplexer #(.width(32)) multiplexer_4 (
    .in0({32{1'b0}}), .in1(multiplier_1_out), .out(multiplexer_4_out), .sel(and_6_out));
  and and_6 (and_6_out, t1, MUL);
  Multiplexer #(.width(32)) multiplexer_5 (
    .in0({32{1'b0}}), .in1(divider_1_out), .out(multiplexer_5_out), .sel(and_7_out));
  and and_7 (and_7_out, t1, DIV);
  Multiplexer #(.width(32)) multiplexer_6 (
    .in0({32{1'b0}}), .in1(negator_1_out), .out(multiplexer_6_out), .sel(and_8_out));
  and and_8 (and_8_out, t1, NEG);
  Multiplexer #(.width(32)) multiplexer_7 (.in0({32{1'b0}}), .in1(and_3_out), .out(multiplexer_7_out), .sel(and_9_out));
  and and_9 (and_9_out, t1, ANDop);
  Multiplexer #(.width(32)) multiplexer_8 (.in0({32{1'b0}}), .in1(or_1_out), .out(multiplexer_8_out), .sel(and_10_out));
  and and_10 (and_10_out, t1, ORop);
  Multiplexer #(.width(32)) multiplexer_9 (
    .in0({32{1'b0}}), .in1(not_1_out), .out(multiplexer_9_out), .sel(and_11_out));
  and and_11 (and_11_out, t1, NOTop);
  S_R_Flip_Flop s_r_ff_1 (.S(and_1_out), .R(1'b0), .clk(clk), .Q(Stop_Lamp), .Qn(s_r_ff_1_qn));  // open: reset, preset
  Register #(.trigger("falling"), .width(32)) IR (
    .D({ram_1_dout_2, ram_1_dout}), .en(t1), .clk(clk), .Q(IR_q));  // open: clr
  and and_12 (and_12_out, clk, s_r_ff_1_qn);
  assign or_2_out = multiplexer_1_out | multiplexer_2_out | multiplexer_3_out | multiplexer_4_out | multiplexer_5_out | multiplexer_6_out | multiplexer_7_out | multiplexer_8_out | multiplexer_9_out;  // OR_Gate or_2, 32 bits wide
  Counter #(.max('h1), .trigger("falling"), .width(1)) CTR3 (
    .clk(and_12_out), .Q(CTR3_q));  // open: clr, load, up, count, D, carry
  Register #(.width(32)) Acc (.D(or_2_out), .en(or_3_out), .clk(clk), .Q(Acc_q));  // open: clr
  or or_3 (or_3_out, and_2_out, and_4_out, and_5_out, and_6_out, and_7_out, and_8_out, and_9_out, and_10_out, and_11_out);
  Decoder #(.select(4)) decoder_1 (
    .out1(JMP), .out2(JRP), .out3(LDN), .out4(STO), .out5(SKN), .out6(SUB), .out7(ADD), .out8(MUL),
    .out9(DIV), .out10(NEG), .out11(ANDop), .out12(ORop), .out13(NOTop), .out14(HLT), .sel(IR_q[19:16]));  // open: out0, out15, en
  LED led_1 (.in(branch_taken));
  and and_13 (branch_taken, comparator_1_lt, SKN);
  Comparator #(.width(32)) comparator_1 (.a(Acc_q), .b({32{1'b0}}), .lt(comparator_1_lt));  // open: gt, eq
  Decoder decoder_2 (.out0(t0), .out1(t1), .sel(CTR3_q));  // open: en
  Adder #(.width(16)) adder_2 (.a(ram_1_dout), .b(PC_q), .out(adder_2_out));  // open: cin, cout
  Adder #(.width(16)) adder_3 (.a(16'h1), .b(PC_q), .out(adder_3_out));  // open: cin, cout
  Adder #(.width(16)) adder_4 (.a(PC_q), .b(16'h2), .out(adder_4_out));  // open: cin, cout
  not not_2 (not_2_out, JMP);
  // NOT_Gate not_3 has open pins: in=branch_taken, out=open
  not not_4 (not_4_out, JRP);
  or or_4 (or_4_out, STO, LDN, SUB, ADD, MUL, DIV, NEG, ANDop, ORop, NOTop);
  Multiplexer #(.width(16)) multiplexer_10 (
    .in1(adder_3_out), .out(multiplexer_10_out), .sel(and_14_out));  // open: in0
  and and_14 (and_14_out, not_2_out, not_4_out);
  Multiplexer #(.width(16)) multiplexer_11 (
    .in0({16{1'b0}}), .in1(adder_4_out), .out(multiplexer_11_out), .sel(and_15_out));
  and and_15 (and_15_out, branch_taken, t0);
  Multiplexer #(.width(16)) multiplexer_12 (
    .in0({16{1'b0}}), .in1(ram_1_dout), .out(multiplexer_12_out), .sel(and_16_out));
  and and_16 (and_16_out, JMP, t0);
  Multiplexer #(.width(16)) multiplexer_13 (
    .in0({16{1'b0}}), .in1(adder_2_out), .out(multiplexer_13_out), .sel(and_17_out));
  and and_17 (and_17_out, JRP, t0);
  Multiplexer #(.width(16)) multiplexer_14 (.in0({16{1'b0}}), .in1(PC_q), .out(multiplexer_14_out), .sel(and_18_out));
  and and_18 (and_18_out, or_4_out, t1);
  assign or_5_out = multiplexer_10_out | multiplexer_11_out | multiplexer_12_out | multiplexer_13_out | multiplexer_14_out;  // OR_Gate or_5, 16 bits wide
  Register #(.trigger("falling"), .width(16)) PC (.D(or_5_out), .en(t0), .clk(clk), .Q(PC_q));  // open: clr
  or or_6 (or_6_out, JMP, JRP);
  or or_7 (or_7_out, SUB, ADD, MUL, DIV, NEG, ANDop, ORop, NOTop);
  and and_19 (and_19_out, t0, or_6_out);
  Multiplexer #(.width(16)) multiplexer_15 (
    .in0({16{1'b0}}), .in1(IR_q[15:0]), .out(multiplexer_15_out), .sel(and_20_out));
  not not_5 (not_5_out, and_20_out);
  and and_20 (and_20_out, t0, LDN);
  Multiplexer #(.width(16)) multiplexer_16 (
    .in0({16{1'b0}}), .in1(IR_q[15:0]), .out(multiplexer_16_out), .sel(and_21_out));
  not not_6 (not_6_out, and_21_out);
  and and_21 (and_21_out, t0, STO);
  Multiplexer #(.width(16)) multiplexer_17 (
    .in0({16{1'b0}}), .in1(IR_q[15:0]), .out(multiplexer_17_out), .sel(and_22_out));
  not not_7 (not_7_out, and_22_out);
  and and_22 (and_22_out, t0, or_7_out);
  Multiplexer #(.width(16)) multiplexer_18 (
    .in0({16{1'b0}}), .in1(IR_q[15:0]), .out(multiplexer_18_out), .sel(and_19_out));
  and and_23 (and_23_out, t1, not_5_out, not_6_out, not_7_out, not_8_out);
  not not_8 (not_8_out, and_19_out);
  Multiplexer #(.width(16)) multiplexer_19 (.in0({16{1'b0}}), .in1(PC_q), .out(multiplexer_19_out), .sel(and_23_out));
  assign or_8_out = multiplexer_19_out | multiplexer_15_out | multiplexer_16_out | multiplexer_17_out | multiplexer_18_out;  // OR_Gate or_8, 16 bits wide
  RAM #(.addrWidth(16), .dataWidth(32)) ram_1 (
    .addr(or_8_out), .we(and_21_out), .oe(1'b1), .clk(clk), .din(Acc_q), .dout({ram_1_dout_2, ram_1_dout}));
endmodule
